// Logisim project HALF ADDER.circ as structural Verilog: 1 circuit, main circuit main
module main (
  input  in_1,
  input  in_2,
  input  in_3,
  input  in_4
);

  wire and_1_out, xor_1_out;

  xor xor_1 (xor_1_out, in_1, in_3);
  and and_1 (and_1_out, in_1, in_3);
endmodule
